// Logisim project muxrisccore.circ as structural Verilog: 1 circuit, main circuit core
module core (
);

  wire adder_1_cout, and_1_out, and_2_out, and_3_out, and_4_out, bitselector_8_out, bitselector_9_out,
       clock_1_out, clock_2_out, clock_3_out, clock_6_out, comparator_1_eq, comparator_2_eq, comparator_3_eq,
       comparator_4_eq, comparator_5_eq, comparator_6_eq, comparator_6_lt, comparator_7_eq, comparator_8_eq,
       comparator_9_eq, comparator_10_eq, comparator_11_eq, comparator_11_gt, comparator_11_lt,
       comparator_12_eq, fpclassificator_1_p2, fpclassificator_1_p3, fpclassificator_1_p4,
       fpclassificator_1_p5, fpclassificator_1_p6, fpclassificator_1_p7, fpcomparator_1_p3,
       fpcomparator_1_p4, multiplexer_1_out, multiplexer_7_out, not_1_out, not_2_out, not_4_out, or_1_out,
       ram1_p4, regY_p3, regY_p4, regZ_p4, subtractor_1_bout;
  wire [1:0] bitselector_11_out;
  wire [3:0] bitselector_6_out, bitselector_7_out;
  wire [5:0] bitselector_10_out;
  wire [7:0] bitselector_5_out;
  wire [15:0] bitselector_1_out, bitselector_2_out, bitselector_3_out, bitselector_4_out;
  wire [23:0] bitselector_12_out, bitselector_13_out, counter_2_q;
  wire [31:0] counter_1_q;
  wire [63:0] absolute_1_p1, adder_1_out, and_5_out, bit_extender_1_out, bit_extender_2_out,
       bit_extender_3_out, bit_extender_4_out, bit_extender_5_out, bit_extender_6_out, bit_extender_7_out,
       bit_extender_8_out, buffer_1_out, divider_1_out, divider_1_rem, exponentiator_1_p3,
       exponentiator_1_p4, fpabsolute_1_p1, fpadder_1_out, fpcomparator_1_p1, fpdivider_1_out,
       fpexponentiator_1_p1, fplogarithm_1_p1, fpminmax_1_p1, fpminmax_1_p2, fpmultiplier_1_out,
       fpnegator_1_p2, fpsquareroot_1_p1, fpsubtractor_1_out, fptoint_1_p1, fptoint_2_p1, fptoint_3_p1,
       fptoint_4_p1, fptrigonometry_1_p8, fptrigonometry_1_p9, fptrigonometry_1_p10, fptrigonometry_1_p11,
       fptrigonometry_2_p2, fptrigonometry_2_p3, fptrigonometry_2_p4, fptrigonometry_3_p2,
       fptrigonometry_3_p3, fptrigonometry_3_p4, inttofp_1_p1, minmax_1_p3, minmax_1_p4, multiplexer_2_out,
       multiplexer_3_out, multiplexer_4_out, multiplexer_5_out, multiplexer_6_out, multiplier_1_cout,
       multiplier_1_out, nand_1_out, negator_1_out, nor_1_out, not_3_out, or_2_out, ram1_p6, ram1_p7,
       register_1_q, regX_dout, regY_p5, shifter_1_out, shifter_2_out, shifter_3_out, shifter_4_out,
       shifter_5_out, squareroot_1_p3, squareroot_1_p4, subtractor_1_out, xnor_1_out, xor_1_out;

  BitSelector #(.group(16), .width(64)) bitselector_1 (.in(register_1_q), .out(bitselector_1_out), .sel(2'b11));
  BitSelector #(.group(16), .width(64)) bitselector_2 (.in(register_1_q), .out(bitselector_2_out), .sel(2'b10));
  BitSelector #(.group(16), .width(64)) bitselector_3 (.in(register_1_q), .out(bitselector_3_out), .sel(2'b01));
  BitSelector #(.group(16), .width(64)) bitselector_4 (.in(register_1_q), .out(bitselector_4_out), .sel(2'b00));
  Register #(.trigger("falling"), .width(64)) register_1 (
    .D(ram1_p6), .en(1'b1), .clk(clock_1_out), .Q(register_1_q));  // open: clr
  Clock clock_1 (.out(clock_1_out));
  BitSelector #(.group(8), .width(16)) bitselector_5 (.in(bitselector_4_out), .out(bitselector_5_out), .sel(1'b1));
  BitSelector #(.group(4), .width(16)) bitselector_6 (.in(bitselector_4_out), .out(bitselector_6_out), .sel(2'b01));
  BitSelector #(.group(4), .width(16)) bitselector_7 (.in(bitselector_4_out), .out(bitselector_7_out), .sel(2'b00));
  RAM #(.addrWidth(16), .dataWidth(64), .enables("line")) regX (
    .addr(bitselector_1_out), .we(regY_p3), .clk(clock_2_out), .din(regY_p5), .dout(regX_dout));
  Clock clock_2 (.out(clock_2_out));
  BitSelector #(.width(4)) bitselector_8 (.in(bitselector_6_out), .out(bitselector_8_out), .sel(2'b00));
  BitSelector #(.width(4)) bitselector_9 (.in(bitselector_6_out), .out(bitselector_9_out), .sel(2'b00));
  BitSelector #(.group(6), .width(64)) bitselector_10 (
    .in(fptrigonometry_1_p8), .out(bitselector_10_out), .sel(4'b0000));
  Comparator #(.mode("unsigned"), .width(4)) comparator_1 (
    .a(bitselector_7_out), .b(4'b0000), .eq(comparator_1_eq));  // open: gt, lt
  Counter #(.max('hffffffff), .trigger("falling"), .width(32)) counter_1 (
    .load(or_1_out), .D({32{1'b0}}), .count(comparator_1_eq), .Q(counter_1_q), .clk(clock_3_out));  // open: carry, up, clr
  Clock clock_3 (.out(clock_3_out));
  Comparator #(.mode("unsigned"), .width(4)) comparator_2 (
    .a(bitselector_7_out), .b(4'b0001), .eq(comparator_2_eq));  // open: gt, lt
  Comparator #(.mode("unsigned"), .width(4)) comparator_3 (
    .a(bitselector_7_out), .b(4'b0010), .eq(comparator_3_eq));  // open: gt, lt
  Comparator #(.mode("unsigned"), .width(4)) comparator_4 (
    .a(bitselector_7_out), .b(4'b0011), .eq(comparator_4_eq));  // open: gt, lt
  and and_1 (and_1_out, comparator_4_eq, bitselector_9_out);
  not not_1 (not_1_out, bitselector_9_out);
  Comparator #(.mode("unsigned"), .width(4)) comparator_5 (
    .a(bitselector_7_out), .b(4'b0100), .eq(comparator_5_eq));  // open: gt, lt
  BitSelector #(.group(2), .width(4)) bitselector_11 (.in(bitselector_6_out), .out(bitselector_11_out), .sel(1'b0));
  Comparator #(.width(64)) comparator_6 (
    .a(fpcomparator_1_p1), .b({64{1'b0}}), .eq(comparator_6_eq), .lt(comparator_6_lt));  // open: gt
  // FPComparator #(.fpwidth(64)) fpcomparator_1: pin names not known; wires that end beside it: fpcomparator_1_p1, {64{1'b0}}, fpcomparator_1_p3, fpcomparator_1_p4
  Comparator #(.mode("unsigned"), .width(4)) comparator_7 (
    .a(bitselector_7_out), .b(4'b0101), .eq(comparator_7_eq));  // open: gt, lt
  Adder #(.width(64)) adder_1 (
    .a(fptrigonometry_1_p8), .b(fpcomparator_1_p1), .out(adder_1_out), .cout(adder_1_cout));  // open: cin
  assign bit_extender_1_out = {{63{1'b0}}, adder_1_cout};  // Bit_Extender bit_extender_1
  Comparator #(.mode("unsigned"), .width(4)) comparator_8 (
    .a(bitselector_7_out), .b(4'b0110), .eq(comparator_8_eq));  // open: gt, lt
  Shifter #(.width(64)) shifter_1 (.in(fpcomparator_1_p1), .\dist (bitselector_10_out), .out(shifter_1_out));
  Comparator #(.mode("unsigned"), .width(4)) comparator_9 (
    .a(bitselector_7_out), .b(4'b0111), .eq(comparator_9_eq));  // open: gt, lt
  FPAdder #(.fpwidth(64)) fpadder_1 (.a(fpcomparator_1_p1), .b(fptrigonometry_1_p8), .out(fpadder_1_out));
  Comparator #(.mode("unsigned"), .width(4)) comparator_10 (
    .a(bitselector_7_out), .b(4'b1000), .eq(comparator_10_eq));  // open: gt, lt
  // FPTrigonometry #(.fpwidth(64)) fptrigonometry_1: pin names not known; wires that end beside it: bitselector_1_out, bitselector_2_out, bitselector_3_out, bitselector_5_out, bitselector_6_out, bitselector_7_out, fpcomparator_1_p1, fptrigonometry_1_p8, fptrigonometry_1_p9, fptrigonometry_1_p10, fptrigonometry_1_p11
  Comparator #(.mode("unsigned"), .width(32)) comparator_11 (
    .a(counter_1_q), .b({bitselector_2_out, bitselector_3_out}), .gt(comparator_11_gt),
    .eq(comparator_11_eq), .lt(comparator_11_lt));
  and and_2 (and_2_out, not_1_out, comparator_4_eq);
  Multiplexer #(.select(2)) multiplexer_1 (
    .in0(comparator_6_eq), .in1(comparator_6_lt), .in2(fpcomparator_1_p3), .in3(fpcomparator_1_p4),
    .out(multiplexer_1_out), .sel(bitselector_11_out));
  Multiplexer #(.select(4), .width(64)) multiplexer_2 (
    .in0(adder_1_out), .in1(bit_extender_1_out), .in2(subtractor_1_out), .in3(bit_extender_2_out),
    .in4(multiplier_1_out), .in5(multiplier_1_cout), .in6(divider_1_out), .in7(divider_1_rem),
    .in8(negator_1_out), .in9(exponentiator_1_p4), .in10(exponentiator_1_p3), .in11(squareroot_1_p4),
    .in12(squareroot_1_p3), .in13(minmax_1_p3), .in14(minmax_1_p4), .in15(absolute_1_p1),
    .out(multiplexer_2_out), .sel(bitselector_6_out));
  Subtractor #(.width(64)) subtractor_1 (
    .a(fpcomparator_1_p1), .b(fptrigonometry_1_p8), .out(subtractor_1_out), .bout(subtractor_1_bout));  // open: bin
  Multiplexer #(.select(4), .width(64)) multiplexer_3 (
    .in0(shifter_1_out), .in1(shifter_2_out), .in2(shifter_3_out), .in3(shifter_4_out), .in4(shifter_5_out),
    .in5(buffer_1_out), .in6(not_3_out), .in7(or_2_out), .in8(and_5_out), .in9(nand_1_out), .in10(nor_1_out),
    .in11(xor_1_out), .in12(xnor_1_out), .out(multiplexer_3_out), .sel(bitselector_6_out));  // open: in13, in14, in15
  Shifter #(.shift("lr"), .width(64)) shifter_2 (
    .in(fpcomparator_1_p1), .\dist (bitselector_10_out), .out(shifter_2_out));
  Multiplexer #(.select(4), .width(64)) multiplexer_4 (
    .in0(fpadder_1_out), .in1(fpsubtractor_1_out), .in2(fpmultiplier_1_out), .in3(fpdivider_1_out),
    .in4(fpnegator_1_p2), .in5(inttofp_1_p1), .in6(fptoint_1_p1), .in7(fptoint_2_p1), .in8(fptoint_3_p1),
    .in9(fptoint_4_p1), .in10(fplogarithm_1_p1), .in11(fpexponentiator_1_p1), .in12(fpsquareroot_1_p1),
    .in13(fpminmax_1_p1), .in14(fpminmax_1_p2), .in15(fpabsolute_1_p1), .out(multiplexer_4_out),
    .sel(bitselector_6_out));
  FPSubtractor #(.fpwidth(64)) fpsubtractor_1 (
    .a(fpcomparator_1_p1), .b(fptrigonometry_1_p8), .out(fpsubtractor_1_out));
  Multiplexer #(.select(4), .width(64)) multiplexer_5 (
    .in0(fptrigonometry_1_p9), .in1(fptrigonometry_1_p10), .in2(fptrigonometry_1_p11),
    .in3(fptrigonometry_2_p2), .in4(fptrigonometry_2_p3), .in5(fptrigonometry_2_p4),
    .in6(fptrigonometry_3_p2), .in7(fptrigonometry_3_p3), .in8(fptrigonometry_3_p4),
    .in9(bit_extender_3_out), .in10(bit_extender_4_out), .in11(bit_extender_6_out),
    .in12(bit_extender_5_out), .in13(bit_extender_7_out), .in14(bit_extender_8_out), .out(multiplexer_5_out),
    .sel(bitselector_6_out));  // open: in15
  // FPTrigonometry #(.fpwidth(64), .\type ("arc")) fptrigonometry_2: pin names not known; wires that end beside it: fpcomparator_1_p1, fptrigonometry_2_p2, fptrigonometry_2_p3, fptrigonometry_2_p4
  or or_1 (or_1_out, comparator_11_gt, comparator_11_eq);
  and and_3 (and_3_out, comparator_11_lt, comparator_1_eq);
  Comparator #(.mode("unsigned"), .width(64)) comparator_12 (
    .a(fpcomparator_1_p1), .b({64{1'b0}}), .eq(comparator_12_eq));  // open: gt, lt
  assign bit_extender_2_out = {{63{1'b0}}, subtractor_1_bout};  // Bit_Extender bit_extender_2
  Shifter #(.shift("ar"), .width(64)) shifter_3 (
    .in(fpcomparator_1_p1), .\dist (bitselector_10_out), .out(shifter_3_out));
  FPMultiplier #(.fpwidth(64)) fpmultiplier_1 (
    .a(fpcomparator_1_p1), .b(fptrigonometry_1_p8), .out(fpmultiplier_1_out));
  // FPTrigonometry #(.fpwidth(64), .\type ("hyp")) fptrigonometry_3: pin names not known; wires that end beside it: fpcomparator_1_p1, fptrigonometry_3_p2, fptrigonometry_3_p3, fptrigonometry_3_p4
  not not_2 (not_2_out, comparator_12_eq);
  Multiplexer #(.width(64)) multiplexer_6 (
    .in0({64{1'b0}}), .in1(64'h1), .out(multiplexer_6_out), .sel(multiplexer_1_out));
  Multiplier #(.width(64)) multiplier_1 (
    .a(fpcomparator_1_p1), .b(fptrigonometry_1_p8), .out(multiplier_1_out), .cout(multiplier_1_cout));  // open: cin
  Shifter #(.shift("rl"), .width(64)) shifter_4 (
    .in(fpcomparator_1_p1), .\dist (bitselector_10_out), .out(shifter_4_out));
  FPDivider #(.fpwidth(64)) fpdivider_1 (.a(fpcomparator_1_p1), .b(fptrigonometry_1_p8), .out(fpdivider_1_out));
  // FPClassificator #(.fpwidth(64)) fpclassificator_1: pin names not known; wires that end beside it: fpcomparator_1_p1, fpclassificator_1_p2, fpclassificator_1_p3, fpclassificator_1_p4, fpclassificator_1_p5, fpclassificator_1_p6, fpclassificator_1_p7
  and and_4 (and_4_out, not_2_out, comparator_2_eq);
  Divider #(.mode("twosComplement"), .width(64)) divider_1 (
    .a(fpcomparator_1_p1), .b(fptrigonometry_1_p8), .out(divider_1_out), .rem(divider_1_rem));  // open: upper
  assign not_3_out = ~fpcomparator_1_p1;  // NOT_Gate not_3, 64 bits wide
  assign or_2_out = fpcomparator_1_p1 | fptrigonometry_1_p8;  // OR_Gate or_2, 64 bits wide
  assign buffer_1_out = fpcomparator_1_p1;  // Buffer buffer_1, 64 bits wide
  Shifter #(.shift("rr"), .width(64)) shifter_5 (
    .in(fpcomparator_1_p1), .\dist (bitselector_10_out), .out(shifter_5_out));
  // FPNegator #(.fpwidth(64)) fpnegator_1: pin names not known; wires that end beside it: fpcomparator_1_p1, fpnegator_1_p2, fpcomparator_1_p1
  // IntToFP #(.fpwidth(64), .width(64)) inttofp_1: pin names not known; wires that end beside it: inttofp_1_p1, fpcomparator_1_p1
  assign bit_extender_3_out = {{63{1'b0}}, fpclassificator_1_p2};  // Bit_Extender bit_extender_3
  Multiplexer multiplexer_7 (.in0(and_4_out), .in1(comparator_2_eq), .out(multiplexer_7_out), .sel(bitselector_8_out));
  Negator #(.width(64)) negator_1 (.in(fpcomparator_1_p1), .out(negator_1_out));
  assign nand_1_out = ~(fpcomparator_1_p1 & fptrigonometry_1_p8);  // NAND_Gate nand_1, 64 bits wide
  assign nor_1_out = ~(fpcomparator_1_p1 | fptrigonometry_1_p8);  // NOR_Gate nor_1, 64 bits wide
  assign and_5_out = fpcomparator_1_p1 & fptrigonometry_1_p8;  // AND_Gate and_5, 64 bits wide
  // FPToInt #(.fpwidth(64), .width(64)) fptoint_1: pin names not known; wires that end beside it: fptoint_1_p1, fpcomparator_1_p1
  assign bit_extender_4_out = {{63{1'b0}}, fpclassificator_1_p3};  // Bit_Extender bit_extender_4
  // Exponentiator #(.mode("twosComplement"), .width(64)) exponentiator_1: pin names not known; wires that end beside it: fpcomparator_1_p1, fptrigonometry_1_p8, exponentiator_1_p3, exponentiator_1_p4
  assign xnor_1_out = ~(fpcomparator_1_p1 ^ fptrigonometry_1_p8);  // XNOR_Gate xnor_1, 64 bits wide
  assign xor_1_out = fpcomparator_1_p1 ^ fptrigonometry_1_p8;  // XOR_Gate xor_1, 64 bits wide
  // FPToInt #(.fpwidth(64), .mode("floor"), .width(64)) fptoint_2: pin names not known; wires that end beside it: fptoint_2_p1, fpcomparator_1_p1
  assign bit_extender_5_out = {{63{1'b0}}, fpclassificator_1_p5};  // Bit_Extender bit_extender_5
  assign bit_extender_6_out = {{63{1'b0}}, fpclassificator_1_p4};  // Bit_Extender bit_extender_6
  // SquareRoot #(.width(64)) squareroot_1: pin names not known; wires that end beside it: fpcomparator_1_p1, fptrigonometry_1_p8, squareroot_1_p3, squareroot_1_p4
  // FPToInt #(.fpwidth(64), .mode("ceil"), .width(64)) fptoint_3: pin names not known; wires that end beside it: fptoint_3_p1, fpcomparator_1_p1
  assign bit_extender_7_out = {{63{1'b0}}, fpclassificator_1_p6};  // Bit_Extender bit_extender_7
  // MinMax #(.mode("twosComplement"), .width(64)) minmax_1: pin names not known; wires that end beside it: fpcomparator_1_p1, fptrigonometry_1_p8, minmax_1_p3, minmax_1_p4, fpcomparator_1_p1
  // FPToInt #(.fpwidth(64), .mode("truncate"), .width(64)) fptoint_4: pin names not known; wires that end beside it: fptoint_4_p1, fpcomparator_1_p1, fptrigonometry_1_p8
  assign bit_extender_8_out = {{63{1'b0}}, fpclassificator_1_p7};  // Bit_Extender bit_extender_8
  // DualRAM #(.addrWidth(16), .dataWidth(64), .enables("line"), .\type ("nonvolatile")) regY: pin names not known; wires that end beside it: bitselector_2_out, bitselector_1_out, regY_p3, regY_p4, regY_p5, fpcomparator_1_p1
  Clock clock_4 (.out(regY_p4));
  // Absolute #(.width(64)) absolute_1: pin names not known; wires that end beside it: absolute_1_p1
  // FPLogarithm #(.fpwidth(64)) fplogarithm_1: pin names not known; wires that end beside it: fplogarithm_1_p1, fpcomparator_1_p1, fptrigonometry_1_p8
  // FPExponentiator #(.fpwidth(64)) fpexponentiator_1: pin names not known; wires that end beside it: fpexponentiator_1_p1, fpcomparator_1_p1
  // FPSquareRoot #(.fpwidth(64)) fpsquareroot_1: pin names not known; wires that end beside it: fpsquareroot_1_p1, fpcomparator_1_p1, fptrigonometry_1_p8
  // FPMinMax #(.fpwidth(64)) fpminmax_1: pin names not known; wires that end beside it: fpminmax_1_p1, fpminmax_1_p2, fpcomparator_1_p1
  or or_3 (regY_p3, comparator_3_eq, and_2_out, comparator_5_eq, comparator_7_eq, comparator_8_eq, comparator_9_eq, comparator_10_eq);
  // FPAbsolute #(.fpwidth(64)) fpabsolute_1: pin names not known; wires that end beside it: fpabsolute_1_p1
  Multiplexer #(.select(4), .width(64)) multiplexer_8 (
    .in0(ram1_p6), .in1(ram1_p6), .in2({{32{1'b0}}, bitselector_2_out, bitselector_3_out}), .in3(ram1_p7),
    .in4(multiplexer_6_out), .in5(multiplexer_2_out), .in6(multiplexer_3_out), .in7(multiplexer_4_out),
    .in8(multiplexer_5_out), .out(regY_p5), .sel(bitselector_7_out));  // open: in9, in10, in11, in12, in13, in14, in15
  BitSelector #(.group(24), .width(64)) bitselector_12 (.in(regX_dout), .out(bitselector_12_out), .sel(2'b00));
  BitSelector #(.group(24), .width(64)) bitselector_13 (.in(fpcomparator_1_p1), .out(bitselector_13_out), .sel(2'b00));
  // DualRAM #(.addrWidth(16), .dataWidth(64), .enables("line"), .\type ("nonvolatile")) regZ: pin names not known; wires that end beside it: bitselector_3_out, bitselector_1_out, regY_p3, regZ_p4, regY_p5, fptrigonometry_1_p8
  Clock clock_5 (.out(regZ_p4));
  Counter #(.max('hffffff), .width(24)) counter_2 (
    .load(multiplexer_7_out), .D(bitselector_12_out), .count(not_4_out), .Q(counter_2_q), .clk(clock_6_out));  // open: carry, up, clr
  not not_4 (not_4_out, and_3_out);
  Clock clock_6 (.out(clock_6_out));
  // DualRAM #(.addrWidth(24), .dataWidth(64), .enables("line"), .\type ("nonvolatile")) ram1: pin names not known; wires that end beside it: counter_2_q, bitselector_13_out, and_1_out, ram1_p4, regX_dout, ram1_p6, ram1_p7
  Clock clock_7 (.out(ram1_p4));
endmodule
